// Logisim project M3 Circuitos Karin & Ana.circ as structural Verilog: 5 circuits, main circuit main
module main (
  input  in_1,
  input  in_2
);

  wire ana_1_out_4, and_1_out, display_1_a, display_1_b, display_1_c, display_1_d, display_1_e, display_1_f,
       display_1_g, display_2_a, display_2_b, display_2_c, display_2_d, display_2_e, display_2_f,
       display_2_g, karin_1_out_4, not_1_out, t_ff_1_q;
  wire [3:0] ana_1_out_5, karin_1_out_5;

  and and_1 (and_1_out, karin_1_out_4, ana_1_out_4);
  T_Flip_Flop t_ff_1 (.clk(in_1), .T(and_1_out), .Q(t_ff_1_q));  // open: Qn, preset, reset, en
  not not_1 (not_1_out, t_ff_1_q);
  Karin karin_1 (.clock(in_1), .enable(t_ff_1_q), .Set(in_2), .out_4(karin_1_out_4), .out_5(karin_1_out_5));
  Ana ana_1 (.clock(in_1), .enable(not_1_out), .set(in_2), .out_4(ana_1_out_4), .out_5(ana_1_out_5));
  Display display_1 (
    .N3(ana_1_out_5[3]), .N2(ana_1_out_5[2]), .N1(ana_1_out_5[1]), .N0(ana_1_out_5[0]), .a(display_1_a),
    .b(display_1_b), .c(display_1_c), .d(display_1_d), .e(display_1_e), .f(display_1_f), .g(display_1_g));
  _7_Segment_Display u_7_segment_display_1 (
    .g(display_1_g), .f(display_1_f), .a(display_1_a), .b(display_1_b), .e(display_1_e), .d(display_1_d),
    .c(display_1_c));  // open: dp
  Display display_2 (
    .N3(karin_1_out_5[3]), .N2(karin_1_out_5[2]), .N1(karin_1_out_5[1]), .N0(karin_1_out_5[0]),
    .a(display_2_a), .b(display_2_b), .c(display_2_c), .d(display_2_d), .e(display_2_e), .f(display_2_f),
    .g(display_2_g));
  _7_Segment_Display u_7_segment_display_2 (
    .g(display_2_g), .f(display_2_f), .a(display_2_a), .b(display_2_b), .e(display_2_e), .d(display_2_d),
    .c(display_2_c));  // open: dp

  // Notes on the sheet:
  //   Alunas: Karin Araldi e Ana Beatriz da Conceição
  //   1ª Sequência (SA ou Sequencia da Ana)   =  9 - 6 - 4 - 7 - 8 - 1 - 13 - 15 - 5 - 2
  //   2ª Sequência (SK ou Sequencia da Karin) = 14 - 15 - 9 - 5 - 13 - 8 - 6 - 2 - 11 - 4
  //   1ª sequencia
  //   2ª sequencia
endmodule

// S K
module Karin (
  input  clock,
  input  enable,
  input  Set,
  output out_4,
  output [3:0] out_5
);

  wire and_1_out, and_2_out, and_3_out, and_4_out, and_5_out, and_6_out, not_1_out, not_2_out, not_3_out,
       not_4_out, not_5_out, not_6_out, not_7_out, not_8_out, not_9_out, not_10_out, or_1_out, or_2_out,
       or_3_out, or_4_out;

  or or_1 (or_1_out, not_2_out, not_1_out);
  not not_1 (not_1_out, out_5[2]);
  not not_2 (not_2_out, out_5[1]);
  J_K_Flip_Flop #(.trigger("falling")) JK3 (
    .J(or_1_out), .clk(clock), .K(not_3_out), .Q(out_5[3]), .preset(Set), .en(enable));  // open: Qn, reset
  not not_3 (not_3_out, out_5[2]);
  or or_2 (or_2_out, and_2_out, and_1_out);
  and and_1 (and_1_out, out_5[0], out_5[3]);
  and and_2 (and_2_out, not_4_out, out_5[1]);
  not not_4 (not_4_out, out_5[3]);
  J_K_Flip_Flop #(.trigger("falling")) JK2 (
    .J(out_5[3]), .clk(clock), .K(or_2_out), .Q(out_5[2]), .preset(Set), .en(enable));  // open: Qn, reset
  not not_5 (not_5_out, out_5[0]);
  J_K_Flip_Flop #(.trigger("falling")) JK1 (
    .J(not_5_out), .clk(clock), .K(out_5[0]), .Q(out_5[1]), .preset(Set), .en(enable));  // open: Qn, reset
  or or_3 (or_3_out, and_3_out, and_5_out);
  and and_3 (and_3_out, not_7_out, not_6_out);
  not not_6 (not_6_out, out_5[3]);
  not not_7 (not_7_out, out_5[2]);
  and and_4 (and_4_out, not_8_out, out_5[1]);
  and and_5 (and_5_out, out_5[2], out_5[3]);
  not not_8 (not_8_out, out_5[2]);
  J_K_Flip_Flop #(.trigger("falling")) JK0 (
    .J(or_3_out), .clk(clock), .K(or_4_out), .Q(out_5[0]), .en(enable), .reset(Set));  // open: Qn, preset
  or or_4 (or_4_out, and_4_out, and_6_out);
  and and_6 (and_6_out, not_9_out, out_5[2], out_5[3]);
  not not_9 (not_9_out, out_5[1]);
  not not_10 (not_10_out, out_5[0]);
  and and_7 (out_4, out_5[3], out_5[2], out_5[1], not_10_out);
  Hex_Digit_Display hex_digit_display_1 (.value(out_5));  // open: dp
endmodule

// S A
module Ana (
  input  clock,
  input  enable,
  input  set,
  output out_4,
  output [3:0] out_5
);

  wire and_1_out, and_2_out, and_3_out, and_4_out, and_5_out, and_6_out, not_1_out, not_2_out, not_3_out,
       not_4_out, not_5_out, not_6_out, not_7_out, not_8_out, not_9_out, not_10_out, or_1_out, or_2_out,
       or_3_out, or_4_out, or_5_out;

  or or_1 (or_1_out, not_1_out, and_1_out);
  and and_1 (and_1_out, out_5[0], out_5[1]);
  not not_1 (not_1_out, out_5[2]);
  J_K_Flip_Flop #(.trigger("falling")) JK3 (
    .J(or_1_out), .clk(clock), .K(or_2_out), .Q(out_5[3]), .en(enable), .reset(set));  // open: Qn, preset
  or or_2 (or_2_out, not_2_out, out_5[1]);
  not not_2 (not_2_out, out_5[2]);
  and and_2 (and_2_out, out_5[0], not_3_out);
  not not_3 (not_3_out, out_5[3]);
  J_K_Flip_Flop #(.trigger("falling")) JK2 (
    .J(out_5[0]), .clk(clock), .K(and_2_out), .Q(out_5[2]), .preset(set), .en(enable));  // open: Qn, reset
  or or_3 (or_3_out, and_3_out, and_4_out);
  and and_3 (and_3_out, not_4_out, out_5[2]);
  and and_4 (and_4_out, out_5[3], out_5[0]);
  not not_4 (not_4_out, out_5[3]);
  J_K_Flip_Flop #(.trigger("falling")) JK1 (
    .J(or_3_out), .clk(clock), .K(1'b1), .Q(out_5[1]), .preset(set), .en(enable));  // open: Qn, reset
  or or_4 (or_4_out, not_5_out, not_6_out);
  not not_5 (not_5_out, out_5[1]);
  not not_6 (not_6_out, out_5[2]);
  and and_5 (and_5_out, not_7_out, out_5[3]);
  not not_7 (not_7_out, out_5[2]);
  J_K_Flip_Flop #(.trigger("falling")) JK0 (
    .J(or_4_out), .clk(clock), .K(or_5_out), .Q(out_5[0]), .en(enable), .reset(set));  // open: Qn, preset
  or or_5 (or_5_out, and_5_out, and_6_out);
  and and_6 (and_6_out, not_8_out, out_5[2]);
  not not_8 (not_8_out, out_5[3]);
  not not_9 (not_9_out, out_5[2]);
  not not_10 (not_10_out, out_5[1]);
  and and_7 (out_4, out_5[3], not_9_out, not_10_out, out_5[0]);
  Hex_Digit_Display hex_digit_display_1 (.value(out_5));  // open: dp
endmodule

module Display (
  input  N3,
  input  N2,
  input  N1,
  input  N0,
  output a,
  output b,
  output c,
  output d,
  output e,
  output f,
  output g
);

  wire and_1_out, and_2_out, and_3_out, and_4_out, and_5_out, and_6_out, and_7_out, and_8_out, and_9_out,
       and_10_out, and_11_out, and_12_out, and_13_out, and_14_out, and_15_out, and_16_out, and_17_out,
       and_18_out, and_19_out, and_20_out, and_21_out, and_22_out, and_23_out, and_24_out, and_25_out,
       and_26_out, and_27_out, and_28_out, and_29_out, and_30_out, and_31_out, and_32_out, and_33_out,
       and_34_out, and_35_out, not_1_out, not_2_out, not_3_out, not_4_out, not_5_out, not_6_out, not_7_out,
       not_8_out, not_9_out, not_10_out, not_11_out, not_12_out, not_13_out, not_14_out, not_15_out,
       not_16_out, not_17_out, not_18_out, not_19_out, not_20_out, not_21_out, not_22_out, not_23_out,
       not_24_out, not_25_out, not_26_out, not_27_out, not_28_out, not_29_out, not_30_out, not_31_out,
       not_32_out, not_33_out, not_34_out, not_35_out, not_36_out, not_37_out, not_38_out, not_39_out,
       not_40_out, not_41_out, not_42_out, not_43_out, not_44_out;

  not not_1 (not_1_out, N2);
  and and_1 (and_1_out, not_1_out, not_2_out);
  not not_2 (not_2_out, N0);
  not not_3 (not_3_out, N3);
  and and_2 (and_2_out, not_3_out, N1);
  not not_4 (not_4_out, N3);
  and and_3 (and_3_out, not_4_out, N2, N0);
  and and_4 (and_4_out, N2, N1);
  and and_5 (and_5_out, N3, not_5_out, not_6_out);
  not not_5 (not_5_out, N2);
  not not_6 (not_6_out, N1);
  and and_6 (and_6_out, N3, not_7_out);
  not not_7 (not_7_out, N0);
  not not_8 (not_8_out, N3);
  and and_7 (and_7_out, not_8_out, not_9_out);
  not not_9 (not_9_out, N2);
  not not_10 (not_10_out, N3);
  and and_8 (and_8_out, not_10_out, not_11_out, not_12_out);
  not not_11 (not_11_out, N1);
  not not_12 (not_12_out, N0);
  not not_13 (not_13_out, N2);
  and and_9 (and_9_out, not_13_out, not_14_out);
  not not_14 (not_14_out, N0);
  not not_15 (not_15_out, N3);
  and and_10 (and_10_out, not_15_out, N1, N0);
  not not_16 (not_16_out, N1);
  and and_11 (and_11_out, N3, not_16_out, N0);
  not not_17 (not_17_out, N3);
  and and_12 (and_12_out, not_17_out, not_18_out);
  not not_18 (not_18_out, N1);
  not not_19 (not_19_out, N3);
  and and_13 (and_13_out, not_19_out, N0);
  not not_20 (not_20_out, N1);
  and and_14 (and_14_out, not_20_out, N0);
  not not_21 (not_21_out, N3);
  and and_15 (and_15_out, not_21_out, N2);
  and and_16 (and_16_out, N3, not_22_out);
  not not_22 (not_22_out, N2);
  not not_23 (not_23_out, N3);
  and and_17 (and_17_out, not_23_out, not_24_out, not_25_out);
  not not_24 (not_24_out, N2);
  not not_25 (not_25_out, N0);
  not not_26 (not_26_out, N2);
  and and_18 (and_18_out, not_26_out, N1, N0);
  not not_27 (not_27_out, N1);
  and and_19 (and_19_out, N2, not_27_out, N0);
  and and_20 (and_20_out, N2, N1, not_28_out);
  not not_28 (not_28_out, N0);
  and and_21 (and_21_out, N3, not_29_out, not_30_out);
  not not_29 (not_29_out, N1);
  not not_30 (not_30_out, N0);
  not not_31 (not_31_out, N2);
  and and_22 (and_22_out, not_31_out, not_32_out);
  not not_32 (not_32_out, N0);
  and and_23 (and_23_out, N1, not_33_out);
  not not_33 (not_33_out, N0);
  and and_24 (and_24_out, N3, N1);
  and and_25 (and_25_out, N3, N2);
  not not_34 (not_34_out, N1);
  and and_26 (and_26_out, not_34_out, not_35_out);
  not not_35 (not_35_out, N0);
  not not_36 (not_36_out, N3);
  and and_27 (and_27_out, not_36_out, N2, not_37_out);
  not not_37 (not_37_out, N1);
  and and_28 (and_28_out, N2, not_38_out);
  not not_38 (not_38_out, N0);
  and and_29 (and_29_out, N3, not_39_out);
  not not_39 (not_39_out, N2);
  and and_30 (and_30_out, N3, N1);
  not not_40 (not_40_out, N2);
  and and_31 (and_31_out, not_40_out, N1);
  and and_32 (and_32_out, N1, not_41_out);
  not not_41 (not_41_out, N0);
  not not_42 (not_42_out, N3);
  and and_33 (and_33_out, not_42_out, N2, not_43_out);
  not not_43 (not_43_out, N1);
  and and_34 (and_34_out, N3, not_44_out);
  not not_44 (not_44_out, N2);
  and and_35 (and_35_out, N3, N0);
  or or_1 (b, and_7_out, and_8_out, and_9_out, and_10_out, and_11_out);
  or or_2 (c, and_12_out, and_13_out, and_14_out, and_15_out, and_16_out);
  or or_3 (d, and_17_out, and_18_out, and_19_out, and_20_out, and_21_out);
  or or_4 (e, and_22_out, and_23_out, and_24_out, and_25_out);
  or or_5 (f, and_26_out, and_27_out, and_28_out, and_29_out, and_30_out);
  or or_6 (g, and_31_out, and_32_out, and_33_out, and_34_out, and_35_out);
  or or_7 (a, and_1_out, and_2_out, and_3_out, and_4_out, and_5_out, and_6_out);
endmodule

module Display_conectado_para_guia (
  input  in_1,
  input  in_2,
  input  in_3,
  input  in_4
);

  wire display_1_a, display_1_b, display_1_c, display_1_d, display_1_e, display_1_f, display_1_g;

  Display display_1 (
    .N3(in_1), .N2(in_2), .N1(in_3), .N0(in_4), .a(display_1_a), .b(display_1_b), .c(display_1_c),
    .d(display_1_d), .e(display_1_e), .f(display_1_f), .g(display_1_g));
  _7_Segment_Display u_7_segment_display_1 (
    .g(display_1_g), .f(display_1_f), .a(display_1_a), .b(display_1_b), .e(display_1_e), .d(display_1_d),
    .c(display_1_c));  // open: dp
endmodule
